// Logisim project Design_Project_MealeyMachine.circ as structural Verilog: 1 circuit, main circuit main
module main (
  input  Sync,
  input  Data,
  output out_3,
  output out_4
);

  wire and_1_out, and_2_out, and_3_out, and_4_out, and_5_out, and_6_out, clock_1_out, j_k_ff_1_q, j_k_ff_2_q,
       not_1_out, not_2_out, not_3_out, or_1_out;

  and and_1 (and_1_out, Data, j_k_ff_2_q);
  or or_1 (or_1_out, and_1_out, and_2_out);
  Clock clock_1 (.out(clock_1_out));
  not not_1 (not_1_out, Data);
  and and_2 (and_2_out, Data, Sync);
  and and_3 (and_3_out, not_1_out, Sync);
  J_K_Flip_Flop j_k_ff_1 (
    .J(or_1_out), .clk(clock_1_out), .K(and_3_out), .Q(j_k_ff_1_q));  // open: Qn, preset, en, reset
  J_K_Flip_Flop j_k_ff_2 (.J(and_3_out), .clk(clock_1_out), .K(Data), .Q(j_k_ff_2_q));  // open: Qn, preset, en, reset
  and and_4 (and_4_out, Data, Sync);
  and and_5 (and_5_out, j_k_ff_2_q, Data);
  not not_2 (not_2_out, Data);
  and and_6 (and_6_out, j_k_ff_1_q, not_2_out, not_3_out);
  not not_3 (not_3_out, Sync);
  or or_2 (out_4, and_4_out, and_5_out, and_6_out);
  D_Flip_Flop d_ff_1 (.clk(clock_1_out), .D(out_4), .Q(out_3));  // open: Qn, preset, en, reset
endmodule
