// Logisim project Design_Project_MooreMachine.circ as structural Verilog: 1 circuit, main circuit main
module main (
  input  Sync,
  input  Data,
  output out_3
);

  wire and_1_out, clock_1_out, j_k_ff_1_q, j_k_ff_2_q, not_1_out, not_2_out;

  Clock clock_1 (.out(clock_1_out));
  not not_1 (not_1_out, Sync);
  and and_1 (and_1_out, not_1_out, j_k_ff_2_q);
  J_K_Flip_Flop j_k_ff_1 (.J(and_1_out), .clk(clock_1_out), .K(Sync), .Q(j_k_ff_1_q));  // open: Qn, preset, en, reset
  not not_2 (not_2_out, Data);
  J_K_Flip_Flop j_k_ff_2 (.J(Data), .clk(clock_1_out), .K(not_2_out), .Q(j_k_ff_2_q));  // open: Qn, preset, en, reset
  xor xor_1 (out_3, j_k_ff_1_q, j_k_ff_2_q);
endmodule
